// Logisim project CPU.circ as structural Verilog
module main (
  input  Prog,
  input  Bout,
  input  in_3,
  input  in_4,
  input  in_5,
  input  in_6,
  input  in_7,
  input  in_8,
  input  in_9,
  input  in_10,
  input  in_11,
  input  in_12
);

  wire A0, A1, A2, A3, AI, alu_1_o0, alu_1_o1, alu_1_o2, alu_1_o3, alu_1_o4, alu_1_o5, alu_1_o6, alu_1_o7,
       AO, BI, CE, CF, CFO, clk, clock_1_out, CO, dipswitch_1_p1, dipswitch_1_p2, dipswitch_1_p3,
       dipswitch_1_p4, dipswitch_2_p1, dipswitch_2_p2, dipswitch_2_p3, dipswitch_2_p4, dipswitch_2_p5,
       dipswitch_2_p6, dipswitch_2_p7, dipswitch_2_p8, EO, FI, Hlt, II, IO, JC, MI, not_1_out, OI,
       ram128bit_1_o4, ram128bit_1_o5, ram128bit_1_o6, ram128bit_1_o7, ramprogrammer_1_m0,
       ramprogrammer_1_m1, ramprogrammer_1_m2, ramprogrammer_1_m3, ramprogrammer_1_m4, ramprogrammer_1_m5,
       ramprogrammer_1_m6, ramprogrammer_1_m7, ramprogrammer_1_o0, ramprogrammer_1_o1, ramprogrammer_1_o2,
       ramprogrammer_1_o3, register8bit_1_out4, register8bit_1_out5, register8bit_1_out6,
       register8bit_1_out7, register8bit_3_d0, register8bit_3_d1, register8bit_3_d2, register8bit_3_d3,
       register8bit_3_d4, register8bit_3_d5, register8bit_3_d6, register8bit_3_d7, register8bit_4_d0,
       register8bit_4_d1, register8bit_4_d2, register8bit_4_d3, register8bit_4_d4, register8bit_4_d5,
       register8bit_4_d6, register8bit_4_d7, register8bit_5_d0, register8bit_5_d1, register8bit_5_d2,
       register8bit_5_d3, register8bit_5_d4, register8bit_5_d5, register8bit_5_d6, register8bit_5_d7, RI, RO,
       SU, writeselect_1_o, WrMem, ZF, ZFO;

  Register8Bit register8bit_1 (
    .In5(register8bit_1_out5), .In6(register8bit_1_out6), .In7(register8bit_1_out7), .In0(ram128bit_1_o7),
    .In1(ram128bit_1_o6), .In2(ram128bit_1_o5), .In3(ram128bit_1_o4), .In4(register8bit_1_out4), .Load(II),
    .Clock(clk), .Enable(IO), .D0(A3), .D1(A2), .D2(A1), .D3(A0), .Out5(register8bit_1_out5),
    .Out6(register8bit_1_out6), .Out7(register8bit_1_out7), .Out4(register8bit_1_out4));  // open: D5, D6, D7, D4, Out0, Out1, Out2, Out3
  Button button_1 (.out(WrMem));
  Register8Bit register8bit_2 (
    .In6(CF), .In7(ZF), .Load(FI), .Clock(clk), .Enable(1'b1), .Out6(CFO), .Out7(ZFO));  // open: In5, In0, In1, In2, In3, In4, D5, D6, D7, D0, D1, D2, D3, D4, Out5, Out0, Out1, Out2, Out3, Out4
  // DipSwitch #(.number(4)) dipswitch_1: pin names not known; wires that end beside it: dipswitch_1_p1, dipswitch_1_p2, dipswitch_1_p3, dipswitch_1_p4
  RamProgrammer ramprogrammer_1 (
    .S(in_3), .Ap3(dipswitch_1_p1), .Ap2(dipswitch_1_p2), .Ap1(dipswitch_1_p3), .Ap0(dipswitch_1_p4),
    .A3(register8bit_1_out4), .A2(register8bit_1_out5), .A1(register8bit_1_out6), .A0(register8bit_1_out7),
    .Load(MI), .Clk(clk), .Dp7(dipswitch_2_p1), .Dp6(dipswitch_2_p2), .Dp5(dipswitch_2_p3),
    .Dp4(dipswitch_2_p4), .Dp3(dipswitch_2_p5), .Dp2(dipswitch_2_p6), .Dp1(dipswitch_2_p7),
    .Dp0(dipswitch_2_p8), .D7(ram128bit_1_o7), .D6(ram128bit_1_o6), .D5(ram128bit_1_o5), .D4(ram128bit_1_o4),
    .D3(register8bit_1_out4), .D2(register8bit_1_out5), .D1(register8bit_1_out6), .D0(register8bit_1_out7),
    .O3(ramprogrammer_1_o3), .O2(ramprogrammer_1_o2), .O1(ramprogrammer_1_o1), .O0(ramprogrammer_1_o0),
    .M7(ramprogrammer_1_m7), .M6(ramprogrammer_1_m6), .M5(ramprogrammer_1_m5), .M4(ramprogrammer_1_m4),
    .M3(ramprogrammer_1_m3), .M2(ramprogrammer_1_m2), .M1(ramprogrammer_1_m1), .M0(ramprogrammer_1_m0));
  RAM128bit ram128bit_1 (
    .D1(ramprogrammer_1_m1), .D0(ramprogrammer_1_m0), .Wr(writeselect_1_o), .A3(ramprogrammer_1_o3),
    .A2(ramprogrammer_1_o2), .A1(ramprogrammer_1_o1), .A0(ramprogrammer_1_o0), .En(RO),
    .D7(ramprogrammer_1_m7), .D6(ramprogrammer_1_m6), .D5(ramprogrammer_1_m5), .D4(ramprogrammer_1_m4),
    .D3(ramprogrammer_1_m3), .D2(ramprogrammer_1_m2), .O2(register8bit_1_out5), .O1(register8bit_1_out6),
    .O0(register8bit_1_out7), .O7(ram128bit_1_o7), .O6(ram128bit_1_o6), .O5(ram128bit_1_o5),
    .O4(ram128bit_1_o4), .O3(register8bit_1_out4));
  // DipSwitch dipswitch_2: pin names not known; wires that end beside it: dipswitch_2_p1, dipswitch_2_p2, dipswitch_2_p3, dipswitch_2_p4, dipswitch_2_p5, dipswitch_2_p6, dipswitch_2_p7, dipswitch_2_p8
  WriteSelect writeselect_1 (.P(in_3), .PS(WrMem), .Rs(RI), .Clk(clk), .O(writeselect_1_o));
  LED led_1 (.in(ram128bit_1_o7));
  LED led_2 (.in(ram128bit_1_o6));
  assign ram128bit_1_o7 = in_4 ? in_5 : 1'bz;  // Controlled_Buffer controlled_buffer_1
  assign ram128bit_1_o6 = in_4 ? in_6 : 1'bz;  // Controlled_Buffer controlled_buffer_2
  LED led_3 (.in(ram128bit_1_o5));
  LED led_4 (.in(ram128bit_1_o4));
  LED led_5 (.in(register8bit_1_out4));
  LED led_6 (.in(register8bit_1_out5));
  assign ram128bit_1_o5 = in_4 ? in_7 : 1'bz;  // Controlled_Buffer controlled_buffer_3
  assign ram128bit_1_o4 = in_4 ? in_8 : 1'bz;  // Controlled_Buffer controlled_buffer_4
  assign register8bit_1_out4 = in_4 ? in_9 : 1'bz;  // Controlled_Buffer controlled_buffer_5
  assign register8bit_1_out5 = in_4 ? in_10 : 1'bz;  // Controlled_Buffer controlled_buffer_6
  LED led_7 (.in(register8bit_1_out6));
  LED led_8 (.in(register8bit_1_out7));
  assign register8bit_1_out6 = in_4 ? in_11 : 1'bz;  // Controlled_Buffer controlled_buffer_7
  assign register8bit_1_out7 = in_4 ? in_12 : 1'bz;  // Controlled_Buffer controlled_buffer_8
  Clock clock_1 (.out(clock_1_out));
  and and_1 (clk, clock_1_out, not_1_out);
  not not_1 (not_1_out, Hlt);
  ProgramCounter programcounter_1 (
    .CE(CE), .Load(JC), .D3(register8bit_1_out4), .D0(register8bit_1_out7), .D1(register8bit_1_out6),
    .D2(register8bit_1_out5), .Clk(clk), .CO(CO), .O3(register8bit_1_out4), .O0(register8bit_1_out7),
    .O1(register8bit_1_out6), .O2(register8bit_1_out5));
  Register8Bit register8bit_3 (
    .In5(register8bit_1_out5), .In6(register8bit_1_out6), .In7(register8bit_1_out7), .In0(ram128bit_1_o7),
    .In1(ram128bit_1_o6), .In2(ram128bit_1_o5), .In3(ram128bit_1_o4), .In4(register8bit_1_out4), .Load(AI),
    .Clock(clk), .Enable(AO), .D5(register8bit_3_d5), .D6(register8bit_3_d6), .D7(register8bit_3_d7),
    .D0(register8bit_3_d0), .D1(register8bit_3_d1), .D2(register8bit_3_d2), .D3(register8bit_3_d3),
    .D4(register8bit_3_d4), .Out5(register8bit_1_out5), .Out6(register8bit_1_out6),
    .Out7(register8bit_1_out7), .Out0(ram128bit_1_o7), .Out1(ram128bit_1_o6), .Out2(ram128bit_1_o5),
    .Out3(ram128bit_1_o4), .Out4(register8bit_1_out4));
  Register8Bit register8bit_4 (
    .In5(register8bit_1_out5), .In6(register8bit_1_out6), .In7(register8bit_1_out7), .In0(ram128bit_1_o7),
    .In1(ram128bit_1_o6), .In2(ram128bit_1_o5), .In3(ram128bit_1_o4), .In4(register8bit_1_out4), .Load(BI),
    .Clock(clk), .Enable(Bout), .D5(register8bit_4_d5), .D6(register8bit_4_d6), .D7(register8bit_4_d7),
    .D0(register8bit_4_d0), .D1(register8bit_4_d1), .D2(register8bit_4_d2), .D3(register8bit_4_d3),
    .D4(register8bit_4_d4), .Out5(register8bit_1_out5), .Out6(register8bit_1_out6),
    .Out7(register8bit_1_out7), .Out0(ram128bit_1_o7), .Out1(ram128bit_1_o6), .Out2(ram128bit_1_o5),
    .Out3(ram128bit_1_o4), .Out4(register8bit_1_out4));
  Register8Bit register8bit_5 (
    .In5(register8bit_1_out5), .In6(register8bit_1_out6), .In7(register8bit_1_out7), .In0(ram128bit_1_o7),
    .In1(ram128bit_1_o6), .In2(ram128bit_1_o5), .In3(ram128bit_1_o4), .In4(register8bit_1_out4), .Load(OI),
    .Clock(clk), .D5(register8bit_5_d5), .D6(register8bit_5_d6), .D7(register8bit_5_d7),
    .D0(register8bit_5_d0), .D1(register8bit_5_d1), .D2(register8bit_5_d2), .D3(register8bit_5_d3),
    .D4(register8bit_5_d4));  // open: Enable, Out5, Out6, Out7, Out0, Out1, Out2, Out3, Out4
  ALU alu_1 (
    .En(EO), .B7(register8bit_4_d0), .A7(register8bit_3_d0), .B6(register8bit_4_d1), .A6(register8bit_3_d1),
    .B5(register8bit_4_d2), .A5(register8bit_3_d2), .A4(register8bit_3_d3), .B4(register8bit_4_d3),
    .B3(register8bit_4_d4), .A3(register8bit_3_d4), .B2(register8bit_4_d5), .A2(register8bit_3_d5),
    .B1(register8bit_4_d6), .A1(register8bit_3_d6), .A0(register8bit_3_d7), .B0(register8bit_4_d7), .SU(SU),
    .S7(ram128bit_1_o7), .S6(ram128bit_1_o6), .S5(ram128bit_1_o5), .S4(ram128bit_1_o4),
    .S3(register8bit_1_out4), .S2(register8bit_1_out5), .S1(register8bit_1_out6), .S0(register8bit_1_out7),
    .O7(alu_1_o7), .O5(alu_1_o5), .O3(alu_1_o3), .O1(alu_1_o1), .O6(alu_1_o6), .O4(alu_1_o4), .O2(alu_1_o2),
    .O0(alu_1_o0), .Cout(CF));
  FourDigitDisplayNew fourdigitdisplaynew_1 (
    .In0(register8bit_5_d7), .In1(register8bit_5_d6), .In2(register8bit_5_d5), .In3(register8bit_5_d4),
    .In4(register8bit_5_d3), .In5(register8bit_5_d2), .In6(register8bit_5_d1), .In7(register8bit_5_d0),
    .Prog(Prog));
  ControlLogic controllogic_1 (
    .Clk(clk), .A0(A0), .A1(A1), .A2(A2), .A3(A3), .CF(CFO), .ZF(ZFO), .Prog(Prog), .J(JC), .CO(CO), .CE(CE),
    .OI(OI), .BI(BI), .SU(SU), .EO(EO), .AO(AO), .AI(AI), .II(II), .IO(IO), .RO(RO), .RI(RI), .MI(MI),
    .Hlt(Hlt), .FI(FI));
  nor nor_1 (ZF, alu_1_o7, alu_1_o6, alu_1_o5, alu_1_o4, alu_1_o3, alu_1_o2, alu_1_o1, alu_1_o0);

  // Other names for the same wires on the sheet: BO = Bout; Program = in_3

  // Notes on the sheet:
  //   Flag Register
  //   Mem Address Register
  //   Memory Out
  //   Memory In
  //   Instruction Register
  //   Program Counter
  //   Register A
  //   Diplay Register
  //   Register B
  //   Control Logic
  //   ALU
  //   Out
  //   (Always On)
endmodule

module Register8Bit (
  input  Load,
  input  Clock,
  input  Enable,
  input  In0,
  input  In1,
  input  In2,
  input  In3,
  input  In4,
  input  In5,
  input  In6,
  input  In7,
  output Out0,
  output D0,
  output Out1,
  output D1,
  output Out2,
  output D2,
  output Out3,
  output D3,
  output Out4,
  output D4,
  output Out5,
  output D5,
  output Out6,
  output D6,
  output Out7,
  output D7
);

  wire and_1_out, and_2_out, and_3_out, and_4_out, and_5_out, and_6_out, and_7_out, and_8_out, and_9_out,
       and_10_out, and_11_out, and_12_out, and_13_out, and_14_out, and_15_out, and_16_out, not_1_out,
       not_2_out, not_3_out, not_4_out, not_5_out, not_6_out, not_7_out, not_8_out, or_1_out, or_2_out,
       or_3_out, or_4_out, or_5_out, or_6_out, or_7_out, or_8_out;

  not not_1 (not_1_out, Load);
  not not_2 (not_2_out, Load);
  not not_3 (not_3_out, Load);
  not not_4 (not_4_out, Load);
  not not_5 (not_5_out, Load);
  not not_6 (not_6_out, Load);
  not not_7 (not_7_out, Load);
  not not_8 (not_8_out, Load);
  and and_1 (and_1_out, D0, not_1_out);
  and and_2 (and_2_out, Load, In0);
  and and_3 (and_3_out, D1, not_2_out);
  and and_4 (and_4_out, Load, In1);
  and and_5 (and_5_out, D2, not_3_out);
  and and_6 (and_6_out, Load, In2);
  and and_7 (and_7_out, D3, not_4_out);
  and and_8 (and_8_out, Load, In3);
  and and_9 (and_9_out, D4, not_5_out);
  and and_10 (and_10_out, Load, In4);
  and and_11 (and_11_out, D5, not_6_out);
  and and_12 (and_12_out, Load, In5);
  and and_13 (and_13_out, D6, not_7_out);
  and and_14 (and_14_out, Load, In6);
  and and_15 (and_15_out, D7, not_8_out);
  and and_16 (and_16_out, Load, In7);
  or or_1 (or_1_out, and_1_out, and_2_out);
  or or_2 (or_2_out, and_3_out, and_4_out);
  or or_3 (or_3_out, and_5_out, and_6_out);
  or or_4 (or_4_out, and_7_out, and_8_out);
  or or_5 (or_5_out, and_9_out, and_10_out);
  or or_6 (or_6_out, and_11_out, and_12_out);
  or or_7 (or_7_out, and_13_out, and_14_out);
  or or_8 (or_8_out, and_15_out, and_16_out);
  D_Flip_Flop d_ff_1 (.D(or_1_out), .clk(Clock), .Q(D0));  // open: Qn, preset, reset
  LED led_1 (.in(D0));
  D_Flip_Flop d_ff_2 (.D(or_2_out), .clk(Clock), .Q(D1));  // open: Qn, preset, reset
  LED led_2 (.in(D1));
  D_Flip_Flop d_ff_3 (.D(or_3_out), .clk(Clock), .Q(D2));  // open: Qn, preset, reset
  LED led_3 (.in(D2));
  D_Flip_Flop d_ff_4 (.D(or_4_out), .clk(Clock), .Q(D3));  // open: Qn, preset, reset
  LED led_4 (.in(D3));
  D_Flip_Flop d_ff_5 (.D(or_5_out), .clk(Clock), .Q(D4));  // open: Qn, preset, reset
  LED led_5 (.in(D4));
  D_Flip_Flop d_ff_6 (.D(or_6_out), .clk(Clock), .Q(D5));  // open: Qn, preset, reset
  LED led_6 (.in(D5));
  D_Flip_Flop d_ff_7 (.D(or_7_out), .clk(Clock), .Q(D6));  // open: Qn, preset, reset
  LED led_7 (.in(D6));
  D_Flip_Flop d_ff_8 (.D(or_8_out), .clk(Clock), .Q(D7));  // open: Qn, preset, reset
  LED led_8 (.in(D7));
  assign Out0 = Enable ? D0 : 1'bz;  // Controlled_Buffer controlled_buffer_1
  assign Out1 = Enable ? D1 : 1'bz;  // Controlled_Buffer controlled_buffer_2
  assign Out2 = Enable ? D2 : 1'bz;  // Controlled_Buffer controlled_buffer_3
  assign Out3 = Enable ? D3 : 1'bz;  // Controlled_Buffer controlled_buffer_4
  assign Out4 = Enable ? D4 : 1'bz;  // Controlled_Buffer controlled_buffer_5
  assign Out5 = Enable ? D5 : 1'bz;  // Controlled_Buffer controlled_buffer_6
  assign Out6 = Enable ? D6 : 1'bz;  // Controlled_Buffer controlled_buffer_7
  assign Out7 = Enable ? D7 : 1'bz;  // Controlled_Buffer controlled_buffer_8
endmodule

module Adder4Bit (
  input  A3,
  input  B3,
  input  A2,
  input  B2,
  input  A1,
  input  B1,
  input  A0,
  input  B0,
  input  Cin,
  output Cout,
  output S3,
  output S2,
  output S1,
  output S0
);

  wire adder1bit_2_cout, adder1bit_3_cout, adder1bit_4_cout;

  Adder1Bit adder1bit_1 (.A(A3), .B(B3), .Cin(adder1bit_2_cout), .S(S3), .Cout(Cout));
  Adder1Bit adder1bit_2 (.A(A2), .B(B2), .Cin(adder1bit_3_cout), .S(S2), .Cout(adder1bit_2_cout));
  Adder1Bit adder1bit_3 (.A(A1), .B(B1), .Cin(adder1bit_4_cout), .S(S1), .Cout(adder1bit_3_cout));
  Adder1Bit adder1bit_4 (.A(A0), .B(B0), .Cin(Cin), .S(S0), .Cout(adder1bit_4_cout));
endmodule

module Adder1Bit (
  input  A,
  input  B,
  input  Cin,
  output S,
  output Cout
);

  wire and_1_out, and_2_out, xor_1_out;

  xor xor_1 (xor_1_out, A, B);
  and and_1 (and_1_out, A, B);
  xor xor_2 (S, xor_1_out, Cin);
  and and_2 (and_2_out, xor_1_out, Cin);
  or or_1 (Cout, and_2_out, and_1_out);
endmodule

module ALU (
  input  A7,
  input  A6,
  input  A5,
  input  A4,
  input  En,
  input  A3,
  input  A2,
  input  A1,
  input  A0,
  input  SU,
  input  B7,
  input  B6,
  input  B5,
  input  B4,
  input  B3,
  input  B2,
  input  B1,
  input  B0,
  output S7,
  output O7,
  output Cout,
  output S6,
  output O6,
  output S5,
  output O5,
  output S4,
  output O4,
  output S3,
  output O3,
  output S2,
  output O2,
  output S1,
  output O1,
  output S0,
  output O0
);

  wire adder4bit_2_cout, xor_1_out, xor_2_out, xor_3_out, xor_4_out, xor_5_out, xor_6_out, xor_7_out,
       xor_8_out;

  assign S7 = En ? O7 : 1'bz;  // Controlled_Buffer controlled_buffer_1
  assign S6 = En ? O6 : 1'bz;  // Controlled_Buffer controlled_buffer_2
  assign S5 = En ? O5 : 1'bz;  // Controlled_Buffer controlled_buffer_3
  assign S4 = En ? O4 : 1'bz;  // Controlled_Buffer controlled_buffer_4
  assign S3 = En ? O3 : 1'bz;  // Controlled_Buffer controlled_buffer_5
  assign S2 = En ? O2 : 1'bz;  // Controlled_Buffer controlled_buffer_6
  assign S1 = En ? O1 : 1'bz;  // Controlled_Buffer controlled_buffer_7
  assign S0 = En ? O0 : 1'bz;  // Controlled_Buffer controlled_buffer_8
  Adder4Bit adder4bit_1 (
    .A3(xor_1_out), .B3(A7), .A2(xor_2_out), .B2(A6), .A1(xor_3_out), .B1(A5), .A0(xor_4_out), .B0(A4),
    .Cin(adder4bit_2_cout), .Cout(Cout), .S3(O7), .S2(O6), .S1(O5), .S0(O4));
  xor xor_1 (xor_1_out, B7, SU);
  xor xor_2 (xor_2_out, B6, SU);
  xor xor_3 (xor_3_out, B5, SU);
  xor xor_4 (xor_4_out, B4, SU);
  Adder4Bit adder4bit_2 (
    .A3(xor_5_out), .B3(A3), .A2(xor_6_out), .B2(A2), .A1(xor_7_out), .B1(A1), .A0(xor_8_out), .B0(A0),
    .Cin(SU), .Cout(adder4bit_2_cout), .S3(O3), .S2(O2), .S1(O1), .S0(O0));
  xor xor_5 (xor_5_out, B3, SU);
  xor xor_6 (xor_6_out, B2, SU);
  xor xor_7 (xor_7_out, B1, SU);
  xor xor_8 (xor_8_out, B0, SU);
endmodule

module Decoder4Bit (
  input  In3,
  input  In2,
  input  In1,
  input  In0,
  output Out0,
  output Out1,
  output Out2,
  output Out3,
  output Out4,
  output Out5,
  output Out6,
  output Out7,
  output Out8,
  output Out9,
  output Out10,
  output Out11,
  output Out12,
  output Out13,
  output Out14,
  output Out15
);

  wire not_1_out, not_2_out, not_3_out, not_4_out;

  not not_1 (not_1_out, In3);
  not not_2 (not_2_out, In2);
  not not_3 (not_3_out, In1);
  not not_4 (not_4_out, In0);
  and and_1 (Out0, not_4_out, not_3_out, not_2_out, not_1_out);
  and and_2 (Out1, In0, not_3_out, not_2_out, not_1_out);
  and and_3 (Out2, not_4_out, In1, not_2_out, not_1_out);
  and and_4 (Out3, In0, In1, not_2_out, not_1_out);
  and and_5 (Out4, not_4_out, not_3_out, In2, not_1_out);
  and and_6 (Out5, In0, not_3_out, In2, not_1_out);
  and and_7 (Out6, not_4_out, In1, In2, not_1_out);
  and and_8 (Out7, In0, In1, In2, not_1_out);
  and and_9 (Out8, not_4_out, not_3_out, not_2_out, In3);
  and and_10 (Out9, In0, not_3_out, not_2_out, In3);
  and and_11 (Out10, not_4_out, In1, not_2_out, In3);
  and and_12 (Out11, In0, In1, not_2_out, In3);
  and and_13 (Out12, not_4_out, not_3_out, In2, In3);
  and and_14 (Out13, In0, not_3_out, In2, In3);
  and and_15 (Out14, not_4_out, In1, In2, In3);
  and and_16 (Out15, In0, In1, In2, In3);
endmodule

module RAM128bit (
  input  Wr,
  input  D7,
  input  D6,
  input  D5,
  input  D4,
  input  D3,
  input  D2,
  input  D1,
  input  D0,
  input  A3,
  input  A2,
  input  A1,
  input  A0,
  input  En,
  output O7,
  output O6,
  output O5,
  output O4,
  output O3,
  output O2,
  output O1,
  output O0
);

  wire decoder4bit_1_out0, decoder4bit_1_out1, decoder4bit_1_out2, decoder4bit_1_out3, decoder4bit_1_out4,
       decoder4bit_1_out5, decoder4bit_1_out6, decoder4bit_1_out7, decoder4bit_1_out8, decoder4bit_1_out9,
       decoder4bit_1_out10, decoder4bit_1_out11, decoder4bit_1_out12, decoder4bit_1_out13,
       decoder4bit_1_out14, decoder4bit_1_out15, ram8bit_1_out0, ram8bit_1_out1, ram8bit_1_out2,
       ram8bit_1_out3, ram8bit_1_out4, ram8bit_1_out5, ram8bit_1_out6, ram8bit_1_out7;

  Decoder4Bit decoder4bit_1 (
    .In3(A3), .In2(A2), .In1(A1), .In0(A0), .Out0(decoder4bit_1_out0), .Out1(decoder4bit_1_out1),
    .Out2(decoder4bit_1_out2), .Out3(decoder4bit_1_out3), .Out4(decoder4bit_1_out4),
    .Out5(decoder4bit_1_out5), .Out6(decoder4bit_1_out6), .Out7(decoder4bit_1_out7),
    .Out8(decoder4bit_1_out8), .Out9(decoder4bit_1_out9), .Out10(decoder4bit_1_out10),
    .Out11(decoder4bit_1_out11), .Out12(decoder4bit_1_out12), .Out13(decoder4bit_1_out13),
    .Out14(decoder4bit_1_out14), .Out15(decoder4bit_1_out15));
  Ram8Bit ram8bit_1 (
    .Wr(Wr), .En(decoder4bit_1_out0), .In7(D7), .In6(D6), .In5(D5), .In4(D4), .In3(D3), .In2(D2), .In1(D1),
    .In0(D0), .Out7(ram8bit_1_out7), .Out6(ram8bit_1_out6), .Out5(ram8bit_1_out5), .Out4(ram8bit_1_out4),
    .Out3(ram8bit_1_out3), .Out2(ram8bit_1_out2), .Out1(ram8bit_1_out1), .Out0(ram8bit_1_out0));
  Ram8Bit ram8bit_2 (
    .Wr(Wr), .En(decoder4bit_1_out1), .In7(D7), .In6(D6), .In5(D5), .In4(D4), .In3(D3), .In2(D2), .In1(D1),
    .In0(D0), .Out7(ram8bit_1_out7), .Out6(ram8bit_1_out6), .Out5(ram8bit_1_out5), .Out4(ram8bit_1_out4),
    .Out3(ram8bit_1_out3), .Out2(ram8bit_1_out2), .Out1(ram8bit_1_out1), .Out0(ram8bit_1_out0));
  Ram8Bit ram8bit_3 (
    .Wr(Wr), .En(decoder4bit_1_out2), .In7(D7), .In6(D6), .In5(D5), .In4(D4), .In3(D3), .In2(D2), .In1(D1),
    .In0(D0), .Out7(ram8bit_1_out7), .Out6(ram8bit_1_out6), .Out5(ram8bit_1_out5), .Out4(ram8bit_1_out4),
    .Out3(ram8bit_1_out3), .Out2(ram8bit_1_out2), .Out1(ram8bit_1_out1), .Out0(ram8bit_1_out0));
  Ram8Bit ram8bit_4 (
    .Wr(Wr), .En(decoder4bit_1_out3), .In7(D7), .In6(D6), .In5(D5), .In4(D4), .In3(D3), .In2(D2), .In1(D1),
    .In0(D0), .Out7(ram8bit_1_out7), .Out6(ram8bit_1_out6), .Out5(ram8bit_1_out5), .Out4(ram8bit_1_out4),
    .Out3(ram8bit_1_out3), .Out2(ram8bit_1_out2), .Out1(ram8bit_1_out1), .Out0(ram8bit_1_out0));
  Ram8Bit ram8bit_5 (
    .Wr(Wr), .En(decoder4bit_1_out4), .In7(D7), .In6(D6), .In5(D5), .In4(D4), .In3(D3), .In2(D2), .In1(D1),
    .In0(D0), .Out7(ram8bit_1_out7), .Out6(ram8bit_1_out6), .Out5(ram8bit_1_out5), .Out4(ram8bit_1_out4),
    .Out3(ram8bit_1_out3), .Out2(ram8bit_1_out2), .Out1(ram8bit_1_out1), .Out0(ram8bit_1_out0));
  Ram8Bit ram8bit_6 (
    .Wr(Wr), .En(decoder4bit_1_out5), .In7(D7), .In6(D6), .In5(D5), .In4(D4), .In3(D3), .In2(D2), .In1(D1),
    .In0(D0), .Out7(ram8bit_1_out7), .Out6(ram8bit_1_out6), .Out5(ram8bit_1_out5), .Out4(ram8bit_1_out4),
    .Out3(ram8bit_1_out3), .Out2(ram8bit_1_out2), .Out1(ram8bit_1_out1), .Out0(ram8bit_1_out0));
  Ram8Bit ram8bit_7 (
    .Wr(Wr), .En(decoder4bit_1_out6), .In7(D7), .In6(D6), .In5(D5), .In4(D4), .In3(D3), .In2(D2), .In1(D1),
    .In0(D0), .Out7(ram8bit_1_out7), .Out6(ram8bit_1_out6), .Out5(ram8bit_1_out5), .Out4(ram8bit_1_out4),
    .Out3(ram8bit_1_out3), .Out2(ram8bit_1_out2), .Out1(ram8bit_1_out1), .Out0(ram8bit_1_out0));
  Ram8Bit ram8bit_8 (
    .Wr(Wr), .En(decoder4bit_1_out7), .In7(D7), .In6(D6), .In5(D5), .In4(D4), .In3(D3), .In2(D2), .In1(D1),
    .In0(D0), .Out7(ram8bit_1_out7), .Out6(ram8bit_1_out6), .Out5(ram8bit_1_out5), .Out4(ram8bit_1_out4),
    .Out3(ram8bit_1_out3), .Out2(ram8bit_1_out2), .Out1(ram8bit_1_out1), .Out0(ram8bit_1_out0));
  Ram8Bit ram8bit_9 (
    .Wr(Wr), .En(decoder4bit_1_out8), .In7(D7), .In6(D6), .In5(D5), .In4(D4), .In3(D3), .In2(D2), .In1(D1),
    .In0(D0), .Out7(ram8bit_1_out7), .Out6(ram8bit_1_out6), .Out5(ram8bit_1_out5), .Out4(ram8bit_1_out4),
    .Out3(ram8bit_1_out3), .Out2(ram8bit_1_out2), .Out1(ram8bit_1_out1), .Out0(ram8bit_1_out0));
  Ram8Bit ram8bit_10 (
    .Wr(Wr), .En(decoder4bit_1_out9), .In7(D7), .In6(D6), .In5(D5), .In4(D4), .In3(D3), .In2(D2), .In1(D1),
    .In0(D0), .Out7(ram8bit_1_out7), .Out6(ram8bit_1_out6), .Out5(ram8bit_1_out5), .Out4(ram8bit_1_out4),
    .Out3(ram8bit_1_out3), .Out2(ram8bit_1_out2), .Out1(ram8bit_1_out1), .Out0(ram8bit_1_out0));
  Ram8Bit ram8bit_11 (
    .Wr(Wr), .En(decoder4bit_1_out10), .In7(D7), .In6(D6), .In5(D5), .In4(D4), .In3(D3), .In2(D2), .In1(D1),
    .In0(D0), .Out7(ram8bit_1_out7), .Out6(ram8bit_1_out6), .Out5(ram8bit_1_out5), .Out4(ram8bit_1_out4),
    .Out3(ram8bit_1_out3), .Out2(ram8bit_1_out2), .Out1(ram8bit_1_out1), .Out0(ram8bit_1_out0));
  Ram8Bit ram8bit_12 (
    .Wr(Wr), .En(decoder4bit_1_out11), .In7(D7), .In6(D6), .In5(D5), .In4(D4), .In3(D3), .In2(D2), .In1(D1),
    .In0(D0), .Out7(ram8bit_1_out7), .Out6(ram8bit_1_out6), .Out5(ram8bit_1_out5), .Out4(ram8bit_1_out4),
    .Out3(ram8bit_1_out3), .Out2(ram8bit_1_out2), .Out1(ram8bit_1_out1), .Out0(ram8bit_1_out0));
  Ram8Bit ram8bit_13 (
    .Wr(Wr), .En(decoder4bit_1_out12), .In7(D7), .In6(D6), .In5(D5), .In4(D4), .In3(D3), .In2(D2), .In1(D1),
    .In0(D0), .Out7(ram8bit_1_out7), .Out6(ram8bit_1_out6), .Out5(ram8bit_1_out5), .Out4(ram8bit_1_out4),
    .Out3(ram8bit_1_out3), .Out2(ram8bit_1_out2), .Out1(ram8bit_1_out1), .Out0(ram8bit_1_out0));
  Ram8Bit ram8bit_14 (
    .Wr(Wr), .En(decoder4bit_1_out13), .In7(D7), .In6(D6), .In5(D5), .In4(D4), .In3(D3), .In2(D2), .In1(D1),
    .In0(D0), .Out7(ram8bit_1_out7), .Out6(ram8bit_1_out6), .Out5(ram8bit_1_out5), .Out4(ram8bit_1_out4),
    .Out3(ram8bit_1_out3), .Out2(ram8bit_1_out2), .Out1(ram8bit_1_out1), .Out0(ram8bit_1_out0));
  Ram8Bit ram8bit_15 (
    .Wr(Wr), .En(decoder4bit_1_out14), .In7(D7), .In6(D6), .In5(D5), .In4(D4), .In3(D3), .In2(D2), .In1(D1),
    .In0(D0), .Out7(ram8bit_1_out7), .Out6(ram8bit_1_out6), .Out5(ram8bit_1_out5), .Out4(ram8bit_1_out4),
    .Out3(ram8bit_1_out3), .Out2(ram8bit_1_out2), .Out1(ram8bit_1_out1), .Out0(ram8bit_1_out0));
  Ram8Bit ram8bit_16 (
    .Wr(Wr), .En(decoder4bit_1_out15), .In7(D7), .In6(D6), .In5(D5), .In4(D4), .In3(D3), .In2(D2), .In1(D1),
    .In0(D0), .Out7(ram8bit_1_out7), .Out6(ram8bit_1_out6), .Out5(ram8bit_1_out5), .Out4(ram8bit_1_out4),
    .Out3(ram8bit_1_out3), .Out2(ram8bit_1_out2), .Out1(ram8bit_1_out1), .Out0(ram8bit_1_out0));
  LED led_1 (.in(ram8bit_1_out7));
  LED led_2 (.in(ram8bit_1_out6));
  assign O7 = En ? ram8bit_1_out7 : 1'bz;  // Controlled_Buffer controlled_buffer_1
  assign O6 = En ? ram8bit_1_out6 : 1'bz;  // Controlled_Buffer controlled_buffer_2
  LED led_3 (.in(ram8bit_1_out5));
  LED led_4 (.in(ram8bit_1_out4));
  assign O5 = En ? ram8bit_1_out5 : 1'bz;  // Controlled_Buffer controlled_buffer_3
  assign O4 = En ? ram8bit_1_out4 : 1'bz;  // Controlled_Buffer controlled_buffer_4
  LED led_5 (.in(ram8bit_1_out2));
  LED led_6 (.in(ram8bit_1_out3));
  assign O2 = En ? ram8bit_1_out2 : 1'bz;  // Controlled_Buffer controlled_buffer_5
  assign O3 = En ? ram8bit_1_out3 : 1'bz;  // Controlled_Buffer controlled_buffer_6
  LED led_7 (.in(ram8bit_1_out1));
  LED led_8 (.in(ram8bit_1_out0));
  assign O1 = En ? ram8bit_1_out1 : 1'bz;  // Controlled_Buffer controlled_buffer_7
  assign O0 = En ? ram8bit_1_out0 : 1'bz;  // Controlled_Buffer controlled_buffer_8
endmodule

module D_Latch (
  input  D,
  input  En,
  output Q
);

  wire and_1_out, and_2_out, nor_2_out, not_1_out;

  not not_1 (not_1_out, D);
  and and_1 (and_1_out, not_1_out, En);
  and and_2 (and_2_out, En, D);
  nor nor_1 (Q, and_1_out, nor_2_out);
  nor nor_2 (nor_2_out, Q, and_2_out);
endmodule

module Ram8Bit (
  input  In7,
  input  In6,
  input  In5,
  input  In4,
  input  In3,
  input  In2,
  input  In1,
  input  In0,
  input  Wr,
  input  En,
  output Out7,
  output Out6,
  output Out5,
  output Out4,
  output Out3,
  output Out2,
  output Out1,
  output Out0
);

  wire and_1_out, d_latch_1_q, d_latch_2_q, d_latch_3_q, d_latch_4_q, d_latch_5_q, d_latch_6_q, d_latch_7_q,
       d_latch_8_q;

  and and_1 (and_1_out, Wr, En);
  D_Latch d_latch_1 (.D(In7), .En(and_1_out), .Q(d_latch_1_q));
  D_Latch d_latch_2 (.D(In6), .En(and_1_out), .Q(d_latch_2_q));
  assign Out7 = En ? d_latch_1_q : 1'bz;  // Controlled_Buffer controlled_buffer_1
  D_Latch d_latch_3 (.D(In5), .En(and_1_out), .Q(d_latch_3_q));
  assign Out6 = En ? d_latch_2_q : 1'bz;  // Controlled_Buffer controlled_buffer_2
  D_Latch d_latch_4 (.D(In4), .En(and_1_out), .Q(d_latch_4_q));
  assign Out5 = En ? d_latch_3_q : 1'bz;  // Controlled_Buffer controlled_buffer_3
  D_Latch d_latch_5 (.D(In3), .En(and_1_out), .Q(d_latch_5_q));
  assign Out4 = En ? d_latch_4_q : 1'bz;  // Controlled_Buffer controlled_buffer_4
  D_Latch d_latch_6 (.D(In2), .En(and_1_out), .Q(d_latch_6_q));
  assign Out3 = En ? d_latch_5_q : 1'bz;  // Controlled_Buffer controlled_buffer_5
  assign Out2 = En ? d_latch_6_q : 1'bz;  // Controlled_Buffer controlled_buffer_6
  D_Latch d_latch_7 (.D(In1), .En(and_1_out), .Q(d_latch_7_q));
  assign Out1 = En ? d_latch_7_q : 1'bz;  // Controlled_Buffer controlled_buffer_7
  D_Latch d_latch_8 (.D(In0), .En(and_1_out), .Q(d_latch_8_q));
  assign Out0 = En ? d_latch_8_q : 1'bz;  // Controlled_Buffer controlled_buffer_8
endmodule

module Register4Bit (
  input  Load,
  input  Clock,
  input  Enable,
  input  In0,
  input  In1,
  input  In2,
  input  In3,
  output Out0,
  output Out1,
  output Out2,
  output Out3
);

  wire and_1_out, and_2_out, and_3_out, and_4_out, and_5_out, and_6_out, and_7_out, and_8_out, d_ff_1_q,
       d_ff_2_q, d_ff_3_q, d_ff_4_q, not_1_out, not_2_out, not_3_out, not_4_out, or_1_out, or_2_out,
       or_3_out, or_4_out;

  not not_1 (not_1_out, Load);
  not not_2 (not_2_out, Load);
  not not_3 (not_3_out, Load);
  not not_4 (not_4_out, Load);
  and and_1 (and_1_out, d_ff_1_q, not_1_out);
  and and_2 (and_2_out, Load, In0);
  and and_3 (and_3_out, d_ff_2_q, not_2_out);
  and and_4 (and_4_out, Load, In1);
  and and_5 (and_5_out, d_ff_3_q, not_3_out);
  and and_6 (and_6_out, Load, In2);
  and and_7 (and_7_out, d_ff_4_q, not_4_out);
  and and_8 (and_8_out, Load, In3);
  or or_1 (or_1_out, and_1_out, and_2_out);
  or or_2 (or_2_out, and_3_out, and_4_out);
  or or_3 (or_3_out, and_5_out, and_6_out);
  or or_4 (or_4_out, and_7_out, and_8_out);
  D_Flip_Flop d_ff_1 (.D(or_1_out), .clk(Clock), .Q(d_ff_1_q));  // open: Qn, preset, reset
  LED Led0 (.in(d_ff_1_q));
  D_Flip_Flop d_ff_2 (.D(or_2_out), .clk(Clock), .Q(d_ff_2_q));  // open: Qn, preset, reset
  LED Led1 (.in(d_ff_2_q));
  D_Flip_Flop d_ff_3 (.D(or_3_out), .clk(Clock), .Q(d_ff_3_q));  // open: Qn, preset, reset
  LED Led2 (.in(d_ff_3_q));
  D_Flip_Flop d_ff_4 (.D(or_4_out), .clk(Clock), .Q(d_ff_4_q));  // open: Qn, preset, reset
  LED Led3 (.in(d_ff_4_q));
  assign Out0 = Enable ? d_ff_1_q : 1'bz;  // Controlled_Buffer controlled_buffer_1
  assign Out1 = Enable ? d_ff_2_q : 1'bz;  // Controlled_Buffer controlled_buffer_2
  assign Out2 = Enable ? d_ff_3_q : 1'bz;  // Controlled_Buffer controlled_buffer_3
  assign Out3 = Enable ? d_ff_4_q : 1'bz;  // Controlled_Buffer controlled_buffer_4
endmodule

module RamProgrammer (
  input  A3,
  input  A2,
  input  A1,
  input  A0,
  input  Load,
  input  Clk,
  input  Ap3,
  input  Ap2,
  input  Ap1,
  input  Ap0,
  input  Dp7,
  input  Dp6,
  input  Dp5,
  input  Dp4,
  input  Dp3,
  input  Dp2,
  input  Dp1,
  input  Dp0,
  input  D7,
  input  D6,
  input  D5,
  input  D4,
  input  D3,
  input  D2,
  input  D1,
  input  D0,
  input  S,
  output M7,
  output M6,
  output M5,
  output M4,
  output M3,
  output M2,
  output M1,
  output M0,
  output O3,
  output O2,
  output O1,
  output O0
);

  wire not_1_out, register4bit_1_out0, register4bit_1_out1, register4bit_1_out2, register4bit_1_out3;

  not not_1 (not_1_out, S);
  LED Run (.in(not_1_out));
  LED Program (.in(S));
  Selector4Bit selector4bit_1 (
    .S(S), .A3(Ap3), .B3(register4bit_1_out3), .A2(Ap2), .B2(register4bit_1_out2), .A1(Ap1),
    .B1(register4bit_1_out1), .A0(Ap0), .B0(register4bit_1_out0), .O3(O3), .O2(O2), .O1(O1), .O0(O0));
  Register4Bit register4bit_1 (
    .In0(A0), .In1(A1), .In2(A2), .In3(A3), .Load(Load), .Clock(Clk), .Enable(1'b1),
    .Out0(register4bit_1_out0), .Out1(register4bit_1_out1), .Out2(register4bit_1_out2),
    .Out3(register4bit_1_out3));
  LED led_1 (.in(register4bit_1_out3));
  LED led_2 (.in(register4bit_1_out2));
  LED led_3 (.in(register4bit_1_out1));
  LED led_4 (.in(register4bit_1_out0));
  Selector8Bit selector8bit_1 (
    .A1(Dp1), .B1(D1), .A0(Dp0), .B0(D0), .S(S), .A7(Dp7), .B7(D7), .A6(Dp6), .B6(D6), .A5(Dp5), .B5(D5),
    .A4(Dp4), .B4(D4), .A3(Dp3), .B3(D3), .A2(Dp2), .B2(D2), .O1(M1), .O0(M0), .O7(M7), .O6(M6), .O5(M5),
    .O4(M4), .O3(M3), .O2(M2));

  // Notes on the sheet:
  //   Address Out
  //   Address In
  //   Memory Data Out
  //   Memory Data In
endmodule

module Selector1Bit (
  input  A,
  input  S,
  input  B,
  output O
);

  wire and_1_out, and_2_out, not_1_out;

  not not_1 (not_1_out, S);
  and and_1 (and_1_out, S, A);
  and and_2 (and_2_out, B, not_1_out);
  or or_1 (O, and_1_out, and_2_out);
endmodule

module Selector4Bit (
  input  A3,
  input  B3,
  input  A2,
  input  B2,
  input  A1,
  input  B1,
  input  A0,
  input  B0,
  input  S,
  output O3,
  output O2,
  output O1,
  output O0
);

  Selector1Bit selector1bit_1 (.S(S), .A(A3), .B(B3), .O(O3));
  Selector1Bit selector1bit_2 (.S(S), .A(A2), .B(B2), .O(O2));
  Selector1Bit selector1bit_3 (.S(S), .A(A1), .B(B1), .O(O1));
  Selector1Bit selector1bit_4 (.S(S), .A(A0), .B(B0), .O(O0));
endmodule

module Selector8Bit (
  input  A7,
  input  B7,
  input  A6,
  input  B6,
  input  A5,
  input  B5,
  input  A4,
  input  B4,
  input  A3,
  input  B3,
  input  A2,
  input  B2,
  input  A1,
  input  B1,
  input  A0,
  input  B0,
  input  S,
  output O7,
  output O6,
  output O5,
  output O4,
  output O3,
  output O2,
  output O1,
  output O0
);

  Selector1Bit selector1bit_1 (.S(S), .A(A7), .B(B7), .O(O7));
  Selector1Bit selector1bit_2 (.S(S), .A(A6), .B(B6), .O(O6));
  Selector1Bit selector1bit_3 (.S(S), .A(A5), .B(B5), .O(O5));
  Selector1Bit selector1bit_4 (.S(S), .A(A4), .B(B4), .O(O4));
  Selector1Bit selector1bit_5 (.S(S), .A(A3), .B(B3), .O(O3));
  Selector1Bit selector1bit_6 (.S(S), .A(A2), .B(B2), .O(O2));
  Selector1Bit selector1bit_7 (.S(S), .A(A1), .B(B1), .O(O1));
  Selector1Bit selector1bit_8 (.S(S), .A(A0), .B(B0), .O(O0));
endmodule

module WriteSelect (
  input  Clk,
  input  Rs,
  input  PS,
  input  P,
  output O
);

  wire and_1_out, risingedgedetector_1_re;

  Selector1Bit selector1bit_1 (.S(P), .A(PS), .B(and_1_out), .O(O));
  RisingEdgeDetector risingedgedetector_1 (.Clk(Clk), .RE(risingedgedetector_1_re));
  and and_1 (and_1_out, Rs, risingedgedetector_1_re);
endmodule

module RisingEdgeDetector (
  input  Clk,
  output RE
);

  wire not_1_out, not_2_out, not_3_out;

  not not_1 (not_1_out, Clk);
  not not_2 (not_2_out, not_1_out);
  not not_3 (not_3_out, not_2_out);
  and and_1 (RE, Clk, not_3_out);
endmodule

module ProgramCounter (
  input  Clk,
  input  CO,
  input  CE,
  input  Load,
  input  D0,
  input  D1,
  input  D2,
  input  D3,
  output O0,
  output O1,
  output O2,
  output O3
);

  wire and_1_out, and_2_out, and_3_out, and_4_out, and_5_out, and_6_out, and_7_out, and_8_out, and_9_out,
       and_10_out, and_11_out, and_12_out, and_13_out, and_14_out, j_k_ff_1_q, j_k_ff_2_q, j_k_ff_3_q,
       j_k_ff_4_q, not_1_out, not_2_out, not_3_out, not_4_out, not_5_out, not_6_out, not_7_out, not_8_out,
       or_1_out, or_2_out, or_3_out, or_4_out, or_5_out, or_6_out, or_7_out, or_8_out;

  and and_1 (and_1_out, j_k_ff_1_q, j_k_ff_2_q);
  and and_2 (and_2_out, and_1_out, j_k_ff_3_q);
  and and_3 (and_3_out, Load, D0);
  and and_4 (and_4_out, 1'b1, CE, not_1_out);
  not not_1 (not_1_out, Load);
  not not_2 (not_2_out, D0);
  and and_5 (and_5_out, not_2_out, Load);
  and and_6 (and_6_out, Load, D1);
  and and_7 (and_7_out, j_k_ff_1_q, CE, not_3_out);
  not not_3 (not_3_out, Load);
  not not_4 (not_4_out, D1);
  and and_8 (and_8_out, not_4_out, Load);
  and and_9 (and_9_out, Load, D2);
  and and_10 (and_10_out, and_1_out, CE, not_5_out);
  not not_5 (not_5_out, Load);
  not not_6 (not_6_out, D2);
  and and_11 (and_11_out, not_6_out, Load);
  and and_12 (and_12_out, Load, D3);
  and and_13 (and_13_out, and_2_out, CE, not_7_out);
  not not_7 (not_7_out, Load);
  not not_8 (not_8_out, D3);
  and and_14 (and_14_out, not_8_out, Load);
  or or_1 (or_1_out, and_3_out, and_4_out);
  or or_2 (or_2_out, and_4_out, and_5_out);
  or or_3 (or_3_out, and_6_out, and_7_out);
  or or_4 (or_4_out, and_7_out, and_8_out);
  or or_5 (or_5_out, and_9_out, and_10_out);
  or or_6 (or_6_out, and_10_out, and_11_out);
  or or_7 (or_7_out, and_12_out, and_13_out);
  or or_8 (or_8_out, and_13_out, and_14_out);
  J_K_Flip_Flop j_k_ff_1 (.J(or_1_out), .K(or_2_out), .clk(Clk), .Q(j_k_ff_1_q));  // open: Qn, preset, reset
  J_K_Flip_Flop j_k_ff_2 (.J(or_3_out), .K(or_4_out), .clk(Clk), .Q(j_k_ff_2_q));  // open: Qn, preset, reset
  J_K_Flip_Flop j_k_ff_3 (.J(or_5_out), .K(or_6_out), .clk(Clk), .Q(j_k_ff_3_q));  // open: Qn, preset, reset
  J_K_Flip_Flop j_k_ff_4 (.J(or_7_out), .K(or_8_out), .clk(Clk), .Q(j_k_ff_4_q));  // open: Qn, preset, reset
  LED LED0 (.in(j_k_ff_1_q));
  LED LED1 (.in(j_k_ff_2_q));
  LED LED2 (.in(j_k_ff_3_q));
  LED LED3 (.in(j_k_ff_4_q));
  assign O0 = CO ? j_k_ff_1_q : 1'bz;  // Controlled_Buffer controlled_buffer_1
  assign O1 = CO ? j_k_ff_2_q : 1'bz;  // Controlled_Buffer controlled_buffer_2
  assign O2 = CO ? j_k_ff_3_q : 1'bz;  // Controlled_Buffer controlled_buffer_3
  assign O3 = CO ? j_k_ff_4_q : 1'bz;  // Controlled_Buffer controlled_buffer_4
endmodule

module Counter2Bit (
  input  Clk,
  output Out0,
  output Out1
);

  wire t_ff_1_qn;

  T_Flip_Flop t_ff_1 (.T(1'b1), .clk(Clk), .Q(Out0), .Qn(t_ff_1_qn));  // open: reset, preset
  T_Flip_Flop t_ff_2 (.T(1'b1), .clk(t_ff_1_qn), .Q(Out1));  // open: Qn, reset, preset
endmodule

module FourDigitDisplay (
  input  Prog,
  input  In0,
  input  In1,
  input  In2,
  input  In3,
  input  In4,
  input  In5,
  input  In6,
  input  In7,
  input  Clk
);

  wire controlled_buffer_1_out, controlled_buffer_2_out, controlled_buffer_3_out, controlled_buffer_4_out,
       controlled_buffer_5_out, controlled_buffer_6_out, controlled_buffer_7_out, controlled_buffer_8_out,
       controlled_buffer_9_out, controlled_buffer_10_out, controlled_buffer_11_out, controlled_buffer_12_out,
       controlled_buffer_13_out, controlled_buffer_14_out, controlled_buffer_15_out,
       controlled_buffer_16_out, controlled_buffer_17_out, controlled_buffer_18_out,
       controlled_buffer_19_out, controlled_buffer_20_out, controlled_buffer_21_out,
       controlled_buffer_22_out, controlled_buffer_23_out, controlled_buffer_24_out,
       controlled_buffer_25_out, controlled_buffer_26_out, controlled_buffer_27_out,
       controlled_buffer_28_out, controlled_buffer_29_out, controlled_buffer_30_out,
       controlled_buffer_31_out, controlled_buffer_32_out, decoder2bit_1_out0, decoder2bit_1_out1,
       decoder2bit_1_out2, decoder2bit_1_out3;
  wire [6:0] sevensegmap_1_sevenseg;
  wire [9:8] counter2bit_1_out0;

  Counter2Bit counter2bit_1 (.Clk(Clk), .Out0(counter2bit_1_out0[8]), .Out1(counter2bit_1_out0[9]));
  SevenSegMap sevensegmap_1 (
    .Prog(Prog), .val({counter2bit_1_out0, In7, In6, In5, In4, In3, In2, In1, In0}),
    .SevenSeg(sevensegmap_1_sevenseg));
  assign controlled_buffer_1_out = decoder2bit_1_out3 ? sevensegmap_1_sevenseg[6] : 1'bz;  // Controlled_Buffer controlled_buffer_1
  assign controlled_buffer_2_out = decoder2bit_1_out3 ? sevensegmap_1_sevenseg[5] : 1'bz;  // Controlled_Buffer controlled_buffer_2
  assign controlled_buffer_3_out = decoder2bit_1_out3 ? sevensegmap_1_sevenseg[0] : 1'bz;  // Controlled_Buffer controlled_buffer_3
  assign controlled_buffer_4_out = decoder2bit_1_out3 ? sevensegmap_1_sevenseg[1] : 1'bz;  // Controlled_Buffer controlled_buffer_4
  _7_Segment_Display u_7_segment_display_1 (
    .g(controlled_buffer_1_out), .f(controlled_buffer_2_out), .a(controlled_buffer_3_out),
    .b(controlled_buffer_4_out), .e(controlled_buffer_5_out), .d(controlled_buffer_6_out),
    .c(controlled_buffer_7_out), .dp(controlled_buffer_8_out));
  assign controlled_buffer_5_out = decoder2bit_1_out3 ? sevensegmap_1_sevenseg[4] : 1'bz;  // Controlled_Buffer controlled_buffer_5
  assign controlled_buffer_6_out = decoder2bit_1_out3 ? sevensegmap_1_sevenseg[3] : 1'bz;  // Controlled_Buffer controlled_buffer_6
  assign controlled_buffer_7_out = decoder2bit_1_out3 ? sevensegmap_1_sevenseg[2] : 1'bz;  // Controlled_Buffer controlled_buffer_7
  assign controlled_buffer_8_out = decoder2bit_1_out3 ? 1'b0 : 1'bz;  // Controlled_Buffer controlled_buffer_8
  Decoder2bit decoder2bit_1 (
    .In1(counter2bit_1_out0[9]), .In0(counter2bit_1_out0[8]), .Out0(decoder2bit_1_out0),
    .Out1(decoder2bit_1_out1), .Out2(decoder2bit_1_out2), .Out3(decoder2bit_1_out3));
  assign controlled_buffer_9_out = decoder2bit_1_out2 ? sevensegmap_1_sevenseg[6] : 1'bz;  // Controlled_Buffer controlled_buffer_9
  _7_Segment_Display u_7_segment_display_2 (
    .g(controlled_buffer_9_out), .f(controlled_buffer_11_out), .a(controlled_buffer_12_out),
    .b(controlled_buffer_13_out), .e(controlled_buffer_10_out), .d(controlled_buffer_14_out),
    .c(controlled_buffer_15_out), .dp(controlled_buffer_16_out));
  assign controlled_buffer_10_out = decoder2bit_1_out2 ? sevensegmap_1_sevenseg[4] : 1'bz;  // Controlled_Buffer controlled_buffer_10
  assign controlled_buffer_11_out = decoder2bit_1_out2 ? sevensegmap_1_sevenseg[5] : 1'bz;  // Controlled_Buffer controlled_buffer_11
  assign controlled_buffer_12_out = decoder2bit_1_out2 ? sevensegmap_1_sevenseg[0] : 1'bz;  // Controlled_Buffer controlled_buffer_12
  assign controlled_buffer_13_out = decoder2bit_1_out2 ? sevensegmap_1_sevenseg[1] : 1'bz;  // Controlled_Buffer controlled_buffer_13
  assign controlled_buffer_14_out = decoder2bit_1_out2 ? sevensegmap_1_sevenseg[3] : 1'bz;  // Controlled_Buffer controlled_buffer_14
  assign controlled_buffer_15_out = decoder2bit_1_out2 ? sevensegmap_1_sevenseg[2] : 1'bz;  // Controlled_Buffer controlled_buffer_15
  assign controlled_buffer_16_out = decoder2bit_1_out2 ? 1'b0 : 1'bz;  // Controlled_Buffer controlled_buffer_16
  assign controlled_buffer_17_out = decoder2bit_1_out1 ? sevensegmap_1_sevenseg[6] : 1'bz;  // Controlled_Buffer controlled_buffer_17
  assign controlled_buffer_18_out = decoder2bit_1_out1 ? sevensegmap_1_sevenseg[5] : 1'bz;  // Controlled_Buffer controlled_buffer_18
  assign controlled_buffer_19_out = decoder2bit_1_out1 ? sevensegmap_1_sevenseg[0] : 1'bz;  // Controlled_Buffer controlled_buffer_19
  _7_Segment_Display u_7_segment_display_3 (
    .g(controlled_buffer_17_out), .f(controlled_buffer_18_out), .a(controlled_buffer_19_out),
    .b(controlled_buffer_23_out), .e(controlled_buffer_20_out), .d(controlled_buffer_21_out),
    .c(controlled_buffer_22_out), .dp(controlled_buffer_24_out));
  assign controlled_buffer_20_out = decoder2bit_1_out1 ? sevensegmap_1_sevenseg[4] : 1'bz;  // Controlled_Buffer controlled_buffer_20
  assign controlled_buffer_21_out = decoder2bit_1_out1 ? sevensegmap_1_sevenseg[3] : 1'bz;  // Controlled_Buffer controlled_buffer_21
  assign controlled_buffer_22_out = decoder2bit_1_out1 ? sevensegmap_1_sevenseg[2] : 1'bz;  // Controlled_Buffer controlled_buffer_22
  assign controlled_buffer_23_out = decoder2bit_1_out1 ? sevensegmap_1_sevenseg[1] : 1'bz;  // Controlled_Buffer controlled_buffer_23
  assign controlled_buffer_24_out = decoder2bit_1_out1 ? 1'b0 : 1'bz;  // Controlled_Buffer controlled_buffer_24
  assign controlled_buffer_25_out = decoder2bit_1_out0 ? sevensegmap_1_sevenseg[6] : 1'bz;  // Controlled_Buffer controlled_buffer_25
  assign controlled_buffer_26_out = decoder2bit_1_out0 ? sevensegmap_1_sevenseg[5] : 1'bz;  // Controlled_Buffer controlled_buffer_26
  _7_Segment_Display u_7_segment_display_4 (
    .g(controlled_buffer_25_out), .f(controlled_buffer_26_out), .a(controlled_buffer_29_out),
    .b(controlled_buffer_30_out), .e(controlled_buffer_27_out), .d(controlled_buffer_28_out),
    .c(controlled_buffer_31_out), .dp(controlled_buffer_32_out));
  assign controlled_buffer_27_out = decoder2bit_1_out0 ? sevensegmap_1_sevenseg[4] : 1'bz;  // Controlled_Buffer controlled_buffer_27
  assign controlled_buffer_28_out = decoder2bit_1_out0 ? sevensegmap_1_sevenseg[3] : 1'bz;  // Controlled_Buffer controlled_buffer_28
  assign controlled_buffer_29_out = decoder2bit_1_out0 ? sevensegmap_1_sevenseg[0] : 1'bz;  // Controlled_Buffer controlled_buffer_29
  assign controlled_buffer_30_out = decoder2bit_1_out0 ? sevensegmap_1_sevenseg[1] : 1'bz;  // Controlled_Buffer controlled_buffer_30
  assign controlled_buffer_31_out = decoder2bit_1_out0 ? sevensegmap_1_sevenseg[2] : 1'bz;  // Controlled_Buffer controlled_buffer_31
  assign controlled_buffer_32_out = decoder2bit_1_out0 ? 1'b0 : 1'bz;  // Controlled_Buffer controlled_buffer_32
endmodule

module Decoder2bit (
  input  In1,
  input  In0,
  output Out0,
  output Out1,
  output Out2,
  output Out3
);

  wire not_1_out, not_2_out, not_3_out, not_4_out;

  not not_1 (not_1_out, In0);
  not not_2 (not_2_out, In1);
  not not_3 (not_3_out, In1);
  not not_4 (not_4_out, In0);
  and and_1 (Out0, not_1_out, not_2_out);
  and and_2 (Out1, In0, not_3_out);
  and and_3 (Out2, not_4_out, In1);
  and and_4 (Out3, In0, In1);
endmodule

module FourDigitDisplayNew (
  input  Prog,
  input  In0,
  input  In1,
  input  In2,
  input  In3,
  input  In4,
  input  In5,
  input  In6,
  input  In7
);

  wire [6:0] sevensegmap_1_sevenseg, sevensegmap_2_sevenseg, sevensegmap_3_sevenseg, sevensegmap_4_sevenseg;

  SevenSegMap sevensegmap_1 (
    .Prog(Prog), .val({2'b00, In7, In6, In5, In4, In3, In2, In1, In0}), .SevenSeg(sevensegmap_1_sevenseg));
  SevenSegMap sevensegmap_2 (
    .Prog(Prog), .val({2'b01, In7, In6, In5, In4, In3, In2, In1, In0}), .SevenSeg(sevensegmap_2_sevenseg));
  SevenSegMap sevensegmap_3 (
    .Prog(Prog), .val({2'b10, In7, In6, In5, In4, In3, In2, In1, In0}), .SevenSeg(sevensegmap_3_sevenseg));
  SevenSegMap sevensegmap_4 (
    .Prog(Prog), .val({2'b11, In7, In6, In5, In4, In3, In2, In1, In0}), .SevenSeg(sevensegmap_4_sevenseg));
  _7_Segment_Display u_7_segment_display_1 (
    .g(sevensegmap_1_sevenseg[6]), .f(sevensegmap_1_sevenseg[5]), .a(sevensegmap_1_sevenseg[0]),
    .b(sevensegmap_1_sevenseg[1]), .e(sevensegmap_1_sevenseg[4]), .d(sevensegmap_1_sevenseg[3]),
    .c(sevensegmap_1_sevenseg[2]), .dp(1'b0));
  _7_Segment_Display u_7_segment_display_2 (
    .g(sevensegmap_2_sevenseg[6]), .f(sevensegmap_2_sevenseg[5]), .a(sevensegmap_2_sevenseg[0]),
    .b(sevensegmap_2_sevenseg[1]), .e(sevensegmap_2_sevenseg[4]), .d(sevensegmap_2_sevenseg[3]),
    .c(sevensegmap_2_sevenseg[2]), .dp(1'b0));
  _7_Segment_Display u_7_segment_display_3 (
    .g(sevensegmap_3_sevenseg[6]), .f(sevensegmap_3_sevenseg[5]), .a(sevensegmap_3_sevenseg[0]),
    .b(sevensegmap_3_sevenseg[1]), .e(sevensegmap_3_sevenseg[4]), .d(sevensegmap_3_sevenseg[3]),
    .c(sevensegmap_3_sevenseg[2]), .dp(1'b0));
  _7_Segment_Display u_7_segment_display_4 (
    .g(sevensegmap_4_sevenseg[6]), .f(sevensegmap_4_sevenseg[5]), .a(sevensegmap_4_sevenseg[0]),
    .b(sevensegmap_4_sevenseg[1]), .e(sevensegmap_4_sevenseg[4]), .d(sevensegmap_4_sevenseg[3]),
    .c(sevensegmap_4_sevenseg[2]), .dp(1'b0));
endmodule

module RingCounter (
  input  Clk,
  input  Rst,
  output Out0,
  output Out1,
  output Out2,
  output Out3,
  output Out4
);

  D_Flip_Flop d_ff_1 (.D(Out4), .clk(Clk), .Q(Out0), .preset(Rst));  // open: Qn, reset
  LED led_1 (.in(Out0));
  D_Flip_Flop d_ff_2 (.D(Out0), .clk(Clk), .Q(Out1), .reset(Rst));  // open: Qn, preset
  LED led_2 (.in(Out1));
  D_Flip_Flop d_ff_3 (.D(Out1), .clk(Clk), .Q(Out2), .reset(Rst));  // open: Qn, preset
  LED led_3 (.in(Out2));
  D_Flip_Flop d_ff_4 (.D(Out2), .clk(Clk), .Q(Out3), .reset(Rst));  // open: Qn, preset
  LED led_4 (.in(Out3));
  D_Flip_Flop d_ff_5 (.D(Out3), .clk(Clk), .Q(Out4), .reset(Rst));  // open: Qn, preset
  LED led_5 (.in(Out4));
endmodule

module ControlLogic (
  input  Prog,
  input  Clk,
  input  A0,
  input  A1,
  input  A2,
  input  A3,
  input  CF,
  input  ZF,
  output J,
  output CO,
  output CE,
  output OI,
  output BI,
  output SU,
  output EO,
  output AO,
  output AI,
  output II,
  output IO,
  output RO,
  output RI,
  output MI,
  output Hlt,
  output FI
);

  wire not_1_out;
  wire [2:0] counte3bit_1_b0;

  Counte3Bit counte3bit_1 (.Clk(not_1_out), .B0(counte3bit_1_b0[0]), .B1(counte3bit_1_b0[1]), .B2(counte3bit_1_b0[2]));
  LED led_1 (.in(counte3bit_1_b0[0]));
  not not_1 (not_1_out, Clk);
  LED led_2 (.in(counte3bit_1_b0[1]));
  LED led_3 (.in(counte3bit_1_b0[2]));
  ControlLogicCommands controllogiccommands_1 (
    .Prog(Prog), .val({ZF, CF, A3, A2, A1, A0, counte3bit_1_b0}),
    .Controls({FI, Hlt, MI, RI, RO, IO, II, AI, AO, EO, SU, BI, OI, CE, CO, J}));
endmodule

module Counte3Bit (
  input  Clk,
  output B0,
  output B1,
  output B2
);

  wire and_1_out, and_2_out, and_3_out, and_4_out, not_1_out, not_2_out, not_3_out, not_4_out, not_5_out,
       or_1_out, or_2_out;

  not not_1 (not_1_out, B0);
  and and_1 (and_1_out, not_1_out, not_2_out, B2);
  not not_2 (not_2_out, B1);
  not not_3 (not_3_out, and_1_out);
  and and_2 (and_2_out, B0, not_4_out);
  not not_4 (not_4_out, and_1_out);
  not not_5 (not_5_out, and_1_out);
  and and_3 (and_3_out, B1, not_5_out, B0);
  and and_4 (and_4_out, not_3_out, 1'b1);
  or or_1 (or_1_out, and_2_out, and_1_out);
  or or_2 (or_2_out, and_3_out, and_1_out);
  J_K_Flip_Flop j_k_ff_1 (.J(and_4_out), .K(1'b1), .clk(Clk), .Q(B0));  // open: Qn, preset, reset
  J_K_Flip_Flop j_k_ff_2 (.J(and_2_out), .K(or_1_out), .clk(Clk), .Q(B1));  // open: Qn, preset, reset
  J_K_Flip_Flop j_k_ff_3 (.J(and_3_out), .K(or_2_out), .clk(Clk), .Q(B2));  // open: Qn, preset, reset
endmodule

// VHDL entity SevenSegMap, as the project stores it:
--------------------------------------------------------------------------------
-- Project :
-- File    :
-- Autor   :
-- Date    :
--
--------------------------------------------------------------------------------
-- Description :
--
--------------------------------------------------------------------------------

LIBRARY ieee;
USE ieee.std_logic_1164.all;
USE ieee.numeric_std.all;

ENTITY SevenSegMap IS
  PORT (
  ------------------------------------------------------------------------------
    Prog             : IN  std_logic; -- toggle to program the board
    val             : IN  std_logic_vector(9 DOWNTO 0); -- 7-segment number to be displayed
  ------------------------------------------------------------------------------
    SevenSeg        : OUT std_logic_vector(6 DOWNTO 0)  -- output vector example
    );
END SevenSegMap;

--------------------------------------------------------------------------------
--Complete your VHDL description below
--------------------------------------------------------------------------------

ARCHITECTURE TypeArchitecture OF SevenSegMap IS

type vector is array (integer range <>) of std_logic_vector(6 downto 0);
signal digits : vector (0 to 10);
signal decoder : vector (0 to 1023);
signal progState : std_logic := '0';


BEGIN

--sets the 9 available digit values
digits <= ("0111111", "0000110", "1011011", "1001111", "1100110", "1101101", "1111101", "0000111", "1111111", "1100111", "0000000");





-- MAIN DECODER PROCESS BEGINS ---------

sevenSeg_arch: process(val)

	variable address : integer range 0 to 1023 := 0;
	
	begin

	if progState = '1' then
	
		address := to_integer(unsigned(val));
		SevenSeg <= decoder(address);
	
	end if;

end process sevenSeg_arch;


-- PROGRAMMING DECODER VALUES PROCESS BEGINS ------------

programming: process(Prog)	
	begin
		if rising_edge(Prog) then
			--program the ones digit
			ones_place: for k in 0 to 255 loop
				decoder(k) <= digits(k mod 10);
			end loop ones_place;
		
			--programs the tens digits
			tens_place: for k in 0 to 255 loop
				decoder(k+256) <= digits(integer(k/10) mod 10);
			end loop tens_place;
		
			--programs the hundreds digits
			hundreds_place: for k in 0 to 255 loop
				decoder(k+512) <= digits(integer(k/100) mod 10);
			end loop hundreds_place;
		
			--programs the thousands digits
			thousands_place: for k in 0 to 255 loop
				decoder(k+768) <= digits(10);
			end loop thousands_place;
			
			-- track that the decoder values have been programmed
			progState <= '1';
		end if;
end process programming;

END TypeArchitecture;

// VHDL entity ControlLogicCommands, as the project stores it:
--------------------------------------------------------------------------------
-- Project :
-- File    :
-- Autor   :
-- Date    :
--
--------------------------------------------------------------------------------
-- Description :
--
--------------------------------------------------------------------------------

LIBRARY ieee;
USE ieee.std_logic_1164.all;
use ieee.numeric_std.all;

ENTITY ControlLogicCommands IS
  PORT (
  ------------------------------------------------------------------------------
    Prog             : IN  std_logic; -- toggle to program the board
    val             : IN  std_logic_vector(8 DOWNTO 0); -- instruction and counter input
  ------------------------------------------------------------------------------
    Controls        : OUT std_logic_vector(15 DOWNTO 0)  -- output vector example
    );
END ControlLogicCommands;

--------------------------------------------------------------------------------
--Complete your VHDL description below
--------------------------------------------------------------------------------

ARCHITECTURE TypeArchitecture OF ControlLogicCommands IS
type vector is array (integer range <>) of std_logic_vector(15 downto 0);
signal decoder : vector (0 to 511);
signal progState : std_logic := '0';

signal FI  : std_logic_vector(15 downto 0) :="1000000000000000";
signal HLT : std_logic_vector(15 downto 0) :="0100000000000000";
signal MI  : std_logic_vector(15 downto 0) :="0010000000000000";
signal RI  : std_logic_vector(15 downto 0) :="0001000000000000";
signal RO  : std_logic_vector(15 downto 0) :="0000100000000000";
signal IO  : std_logic_vector(15 downto 0) :="0000010000000000";
signal II  : std_logic_vector(15 downto 0) :="0000001000000000";
signal AI  : std_logic_vector(15 downto 0) :="0000000100000000";
signal AO  : std_logic_vector(15 downto 0) :="0000000010000000";
signal EO  : std_logic_vector(15 downto 0) :="0000000001000000";
signal SU  : std_logic_vector(15 downto 0) :="0000000000100000";
signal BI  : std_logic_vector(15 downto 0) :="0000000000010000";
signal OI  : std_logic_vector(15 downto 0) :="0000000000001000";
signal CE  : std_logic_vector(15 downto 0) :="0000000000000100";
signal CO  : std_logic_vector(15 downto 0) :="0000000000000010";
signal J   : std_logic_vector(15 downto 0) :="0000000000000001";
signal NONE: std_logic_vector(15 downto 0) :="0000000000000000";


BEGIN


-- MAIN DECODER PROCESS BEGINS ---------

sevenSeg_arch: process(val, prog)

	variable address : integer range 0 to 511 := 0;
	
	begin

	if progState = '1' then
	
		address := to_integer(unsigned(val));
		Controls <= decoder(address);
	
	end if;

end process sevenSeg_arch;


-- PROGRAMMING DECODER VALUES PROCESS BEGINS ------------

programming: process(Prog)
	variable currentLoc : std_logic_vector(8 DOWNTO 0) := "000000000";
	variable currentCommand : std_logic_vector(3 DOWNTO 0) := "0000";
	variable flags : std_logic_vector(1 DOWNTO 0) := "00";		
	variable currentLocInt : integer range 0 to 511 := 0;	
	begin
		if rising_edge(Prog) then
		
			--program the fetch cycle for all instructions
			fetch: for k in 0 to 511 loop
				if to_unsigned(k,9)(2 DOWNTO 0) = "000" then
					decoder(k) <= MI or CO; --MI and CO pins active
				elsif to_unsigned(k,9)(2 DOWNTO 0) = "001" then
					decoder(k) <= RO or II or CE; --RO, II, and CE pins active
				end if;
			end loop fetch;


			commands: for k in 0 to 3 loop
				--programs the 0000 command (does nothing atm)
				currentCommand:="0000";
				flags:=std_logic_vector(to_unsigned(k,2));
				currentLoc:=flags & currentCommand & "010";
				currentLocInt:=to_integer(unsigned(currentLoc));
				decoder(currentLocInt)   <= NONE;    --No pins active
				decoder(currentLocInt+1) <= NONE;    --No pins active
				decoder(currentLocInt+2) <= NONE;    --No pins active
	
				--programs the A register load command (LDA)
				currentCommand:="0001";
				flags:=std_logic_vector(to_unsigned(k,2));
				currentLoc:=flags & currentCommand & "010";
				currentLocInt:=to_integer(unsigned(currentLoc));
				decoder(currentLocInt)   <= MI or IO;--MI and IO pins active
				decoder(currentLocInt+1) <= RO or AI;--RO and AI pins active
				decoder(currentLocInt+2) <= NONE;    --No pins active
	
				--programs the add command (ADD)
				currentCommand:="0010";
				flags:=std_logic_vector(to_unsigned(k,2));
				currentLoc:=flags & currentCommand & "010";
				currentLocInt:=to_integer(unsigned(currentLoc));
				decoder(currentLocInt)   <= MI or IO;	   --MI and IO pins active
				decoder(currentLocInt+1) <= RO or BI;	   --RO and BI pins active
				decoder(currentLocInt+2) <= AI or EO or FI;--AI and EO pins active
	
				--programs the subtract command (SUB)
				currentCommand:="0011";
				flags:=std_logic_vector(to_unsigned(k,2));
				currentLoc:=flags & currentCommand & "010";
				currentLocInt:=to_integer(unsigned(currentLoc));
				decoder(currentLocInt)   <= MI or IO;      --MI and IO pins active
				decoder(currentLocInt+1) <= RO or BI;      --RO and BI pins active
				decoder(currentLocInt+2) <= AI or EO or SU or FI;--AI and EO and SU pins active
	
				--programs the store A command (STA)
				currentCommand:="0100";
				flags:=std_logic_vector(to_unsigned(k,2));
				currentLoc:=flags & currentCommand & "010";
				currentLocInt:=to_integer(unsigned(currentLoc));
				decoder(currentLocInt)   <= IO or MI;
				decoder(currentLocInt+1) <= AO or RI;
				decoder(currentLocInt+2) <= NONE;
	
				--programs the load immediate commmand (LDI)
				currentCommand:="0101";
				flags:=std_logic_vector(to_unsigned(k,2));
				currentLoc:=flags & currentCommand & "010";
				currentLocInt:=to_integer(unsigned(currentLoc));
				decoder(currentLocInt)   <= IO or AI;
				decoder(currentLocInt+1) <= NONE;
				decoder(currentLocInt+2) <= NONE;
	
				--programs the jump command (JMP)
				currentCommand:="0110";
				flags:=std_logic_vector(to_unsigned(k,2));
				currentLoc:=flags & currentCommand & "010";
				currentLocInt:=to_integer(unsigned(currentLoc));
				decoder(currentLocInt)   <= IO or J;
				decoder(currentLocInt+1) <= NONE;
				decoder(currentLocInt+2) <= NONE;
	
				--programs the conditional jump carry command (JC)
				currentCommand:="0111";
				flags:=std_logic_vector(to_unsigned(k,2));
				currentLoc:=flags & currentCommand & "010";
				currentLocInt:=to_integer(unsigned(currentLoc));
				if flags(0 DOWNTO 0) = "1" then
					decoder(currentLocInt)   <= IO or J;
				else
					decoder(currentLocInt)   <= NONE;    --No pins active
				end if;
				decoder(currentLocInt+1) <= NONE;    --No pins active
				decoder(currentLocInt+2) <= NONE;    --No pins active
	
				--programs the conditional jump zero command (JZ)
				currentCommand:="1000";
				flags:=std_logic_vector(to_unsigned(k,2));
				currentLoc:=flags & currentCommand & "010";
				currentLocInt:=to_integer(unsigned(currentLoc));
				if flags(1 DOWNTO 1) = "1" then
					decoder(currentLocInt)   <= IO or J;
				else
					decoder(currentLocInt)   <= NONE;    --No pins active
				end if;
				decoder(currentLocInt+1) <= NONE;    --No pins active
				decoder(currentLocInt+2) <= NONE;    --No pins active
	
				--programs the 1001 command (does nothing atm)
				currentCommand:="1001";
				flags:=std_logic_vector(to_unsigned(k,2));
				currentLoc:=flags & currentCommand & "010";
				currentLocInt:=to_integer(unsigned(currentLoc));
				decoder(currentLocInt)   <= NONE;    --No pins active
				decoder(currentLocInt+1) <= NONE;    --No pins active
				decoder(currentLocInt+2) <= NONE;    --No pins active
	
				--programs the 1010 command (does nothing atm)
				currentCommand:="1010";
				flags:=std_logic_vector(to_unsigned(k,2));
				currentLoc:=flags & currentCommand & "010";
				currentLocInt:=to_integer(unsigned(currentLoc));
				decoder(currentLocInt)   <= NONE;    --No pins active
				decoder(currentLocInt+1) <= NONE;    --No pins active
				decoder(currentLocInt+2) <= NONE;    --No pins active
	
				--programs the 1011 command (does nothing atm)
				currentCommand:="1011";
				flags:=std_logic_vector(to_unsigned(k,2));
				currentLoc:=flags & currentCommand & "010";
				currentLocInt:=to_integer(unsigned(currentLoc));
				decoder(currentLocInt)   <= NONE;    --No pins active
				decoder(currentLocInt+1) <= NONE;    --No pins active
				decoder(currentLocInt+2) <= NONE;    --No pins active
	
				--programs the 1100 command (does nothing atm)
				currentCommand:="1100";
				flags:=std_logic_vector(to_unsigned(k,2));
				currentLoc:=flags & currentCommand & "010";
				currentLocInt:=to_integer(unsigned(currentLoc));
				decoder(currentLocInt)   <= NONE;    --No pins active
				decoder(currentLocInt+1) <= NONE;    --No pins active
				decoder(currentLocInt+2) <= NONE;    --No pins active
	
				--programs the 1101 command (does nothing atm)
				currentCommand:="1101";
				flags:=std_logic_vector(to_unsigned(k,2));
				currentLoc:=flags & currentCommand & "010";
				currentLocInt:=to_integer(unsigned(currentLoc));
				decoder(currentLocInt)   <= NONE;    --No pins active
				decoder(currentLocInt+1) <= NONE;    --No pins active
				decoder(currentLocInt+2) <= NONE;    --No pins active
	
				--programs the display out command command (OUT)
				currentCommand:="1110";
				flags:=std_logic_vector(to_unsigned(k,2));
				currentLoc:=flags & currentCommand & "010";
				currentLocInt:=to_integer(unsigned(currentLoc));
				decoder(currentLocInt)   <= AO or OI;--AO and OI pins active
				decoder(currentLocInt+1) <= NONE;    --No pins active
				decoder(currentLocInt+2) <= NONE;    --No pins active
	
				--programs the halt command command (HLT)
				currentCommand:="1111";
				flags:=std_logic_vector(to_unsigned(k,2));
				currentLoc:=flags & currentCommand & "010";
				currentLocInt:=to_integer(unsigned(currentLoc));
				decoder(currentLocInt)   <= HLT;   --HLT pin active
				decoder(currentLocInt+1) <= NONE;  --No pins active
				decoder(currentLocInt+2) <= NONE;  --No pins active
			end loop commands;
		
			
			-- track that the decoder values have been programmed
			progState <= '1';
		end if;
end process programming;


END TypeArchitecture;
